# Fritzing sketch prototypeV1 (saved by Fritzing 0.9.3b)
breadboards: 2

parts:
  LCD1 = LCD screen
  Part1 = Arduino Mega 2560 (Rev3)
  R1 = Rotary Potentiometer (Small) [maximum_resistance=10kΩ package=THT]
  S2 = Pushbutton [package="[THT]"]
  S3 = Pushbutton [package="[THT]"]
  M1 = Stepper Motor - Unipolar
  S4 = Toggle Switch [package=THT]
  IC4 = ULN2003A [package="SO16 [SMD]"]
  IC5 = ULN2003A [package="SO16 [SMD]"]
  M2 = Stepper Motor - Unipolar
  R4 = Resistor [tolerance=±5% resistance=4.7k package=THT]
  R5 = Resistor [tolerance=±5% resistance=4.7k package=THT]
  R6 = Resistor [tolerance=±5% resistance=4.7k package=THT]
  R7 = Resistor [tolerance=±5% resistance=4.7k package=THT]
  R8 = Resistor [tolerance=±5% resistance=4.7k package=THT]
  R9 = Resistor [tolerance=±5% resistance=4.7k package=THT]
  R10 = Resistor [tolerance=±5% resistance=4.7k package=THT]
  R11 = Resistor [tolerance=±5% resistance=4.7k package=THT]
  LED1 = LED - 3mm [color="Green (560nm)" package="3 mm [THT]"]
  R12 = Resistor [tolerance=±5% resistance=10k package=THT]
  R13 = Resistor [tolerance=±5% resistance=10k package=THT]
  R14 = Resistor [tolerance=±5% resistance=10k package=THT]
  LED2 = LED - 3mm [color="Yellow (592nm)" package="3 mm [THT]"]
  LED3 = LED - 3mm [color="Red (633nm)" package="3 mm [THT]"]

nets:
  VSS: LCD1.VSS, LCD1.R/W, LCD1.LED-, Part1.GND, R1.leg2, S2.Pin_1, S2.Pin_2, S3.Pin_1, S3.Pin_2, S4.L1, IC4.0V, IC4.Out_7, IC4.Out_6, IC4.Out_5, IC5.0V, IC5.Out_7, IC5.Out_6, IC5.Out_5, R12.Pin_1, R13.Pin_1, R14.Pin_1
  VDD: LCD1.VDD, LCD1.LED+, Part1.5V, R1.leg1, S4.L2
  N1: LCD1.V0, R1.wiper
  N2: LCD1.RS, Part1.D16_PWM/TX2
  N3: LCD1.E, Part1.D17_PWM/RX2
  N4: LCD1.DB4, Part1.D18/TX1
  N5: LCD1.DB5, Part1.D19/RX1
  N6: LCD1.DB6, Part1.D20/SDA
  N7: LCD1.DB7, Part1.D21/SCL
  N8: Part1.A0, S4.COM
  N9: Part1.A1, S2.Pin_3, S2.Pin_4
  N10: Part1.A2, S3.Pin_3, S3.Pin_4
  N11: Part1.D9_PWM, IC4.In_4, R7.Pin_1
  N12: Part1.D8_PWM, IC4.In_3, R4.Pin_1
  N13: Part1.VIN, M1.COMMON_1, M1.COMMON_2, IC4.COM_-_Common, IC5.COM_-_Common, M2.COMMON_1, M2.COMMON_2, R4.Pin_0, R5.Pin_0, R6.Pin_0, R7.Pin_0, R8.Pin_0, R9.Pin_0, R10.Pin_0, R11.Pin_0, LED1.anode, LED2.anode, LED3.anode
  N14: Part1.D2_PWM, IC5.In_1, R8.Pin_1
  N15: Part1.D3_PWM, IC5.In_2, R9.Pin_1
  N16: Part1.D4_PWM, IC5.In_3, R11.Pin_1
  N17: Part1.D5_PWM, IC5.In_4, R10.Pin_1
  N18: Part1.D6_PWM, IC4.In_1, R6.Pin_1
  N19: Part1.D7_PWM, IC4.In_2, R5.Pin_1
  N20: M1.A, IC5.Out_4
  N21: M1.C, IC5.Out_2
  N22: M1.B, IC5.Out_3
  N23: M1.D, IC5.Out_1
  N24: IC4.Out_4, M2.A
  N25: IC4.Out_3, M2.B
  N26: IC4.Out_2, M2.C
  N27: IC4.Out_1, M2.D
  N28: LED1.cathode, R12.Pin_0
  N29: R13.Pin_0, LED2.cathode
  N30: R14.Pin_0, LED3.cathode

notes:
  Prototype V1 Wiring Diagram
  Stepper Controller (implemented with 2x ULN2003 breakout boards)
  (Rotation Stepper)
  (Y-Axis Stepper)
  3D Scanner
  Controls:
  Contrast | Run/Home Mode | Manual Down/Up
  Microcontroller (Arduino Mega 2650)
  <= Display                    Indicator LEDs =>
