# Fritzing sketch prototypeV2 (saved by Fritzing 0.9.3b)
breadboards: 3

parts:
  Part3 = Arduino Mega 2560 (Rev3)
  R25 = Resistor [tolerance=±5% resistance=220 package=THT]
  U5 = Voltage Regulator - 5V [package="DPak [SMD]"]
  RE3 = Rotary Encoder [package=THT]
  hc-sr5 = hc-sr04
  S3 = Pushbutton [package="[THT]"]
  hc-sr6 = hc-sr04
  R26 = Resistor [tolerance=±5% resistance=220 package=THT]
  Pololu_A3 = Pololu A4988 [package=SO16]
  R27 = Resistor [tolerance=±5% resistance=220 package=THT]
  C3 = Electrolytic Capacitor [capacitance=1µF package="100 mil [THT, electrolytic]"]
  Power_plug3 = Power plug
  LCD3 = LCD screen
  R28 = Rotary Potentiometer (Small) [maximum_resistance=100kΩ package=THT]
  M5 = Stepper Motor - Bipolar
  M6 = Stepper Motor - Unipolar
  IC3 = ULN2003A [package="SO16 [SMD]"]
  R29 = Resistor [tolerance=±5% resistance=220 package=THT]
  R30 = Resistor [tolerance=±5% resistance=220 package=THT]
  R31 = Resistor [tolerance=±5% resistance=220 package=THT]
  R32 = Resistor [tolerance=±5% resistance=220 package=THT]
  LED13 = LED - 3mm [color="Red (635nm)" package="3 mm [THT]"]
  LED14 = LED - 3mm [color="Yellow (592nm)" package="3 mm [THT]"]
  LED15 = LED - 3mm [color="Green (560nm)" package="3 mm [THT]"]
  U6 = SWITCH-SPST-2 [package=r_sw_th]
  R33 = Resistor [tolerance=±5% resistance=220 package=THT]
  R34 = Resistor [tolerance=±5% resistance=220 package=THT]
  R35 = Resistor [tolerance=±5% resistance=220 package=THT]
  S6 = Round Pushbutton

nets:
  N1: Part3.A8, LED15.anode
  N2: Part3.A9, LED14.anode
  N3: Part3.A10, LED13.anode
  N4: Part3.A15, S6.leg0
  N5: Part3.A0, S3.Pin_3, S3.Pin_4
  N6: Part3.A1, RE3.EncoderPinB, R26.Pin_1
  N7: Part3.A2, RE3.EncoderPinA, R27.Pin_1
  N8: Part3.A4, hc-sr6.Trig
  N9: Part3.A5, hc-sr6.Echo
  N10: Part3.A6, hc-sr5.Trig
  N11: Part3.A7, hc-sr5.Echo
  N12: Part3.D21/SCL, LCD3.DB7
  N13: Part3.D20/SDA, LCD3.DB6
  N14: Part3.D19/RX1, LCD3.DB5
  N15: Part3.D18/TX1, LCD3.DB3, LCD3.DB4
  N16: Part3.D17_PWM/RX2, LCD3.E
  N17: Part3.D16_PWM/TX2, LCD3.RS
  N18: Part3.D10_PWM, Pololu_A3.DIR
  N19: Part3.D9_PWM, Pololu_A3.STEP
  N20: Part3.D8_PWM, R25.Pin_1, Pololu_A3.SLEEP
  VCC: Part3.5V, U5.output_voltage, hc-sr5.VCC, hc-sr6.VCC, R26.Pin_0, Pololu_A3.RESET, Pololu_A3.VDD, R27.Pin_0, LCD3.VDD, LCD3.LED+, R28.leg2, M6.COMMON_1, M6.COMMON_2, IC3.COM_-_Common, R29.Pin_0, R30.Pin_0, R31.Pin_0, R32.Pin_0
  GND: Part3.GND, R25.Pin_0, U5.GND, RE3.EncoderPinC, hc-sr5.GND, hc-sr6.GND, Pololu_A3.GND, C3.-, Power_plug3.GND, LCD3.VSS, LCD3.R/W, LCD3.LED-, R28.leg1, IC3.0V, IC3.Out_7, IC3.Out_6, IC3.Out_5, R33.Pin_1, R34.Pin_1, R35.Pin_1, S6.leg1
  N21: Part3.D2_PWM, IC3.In_1, R30.Pin_1
  N22: Part3.D3_PWM, IC3.In_2, R29.Pin_1
  N23: Part3.D4_PWM, IC3.In_3, R31.Pin_1
  N24: Part3.D5_PWM, IC3.In_4, R32.Pin_1
  N25: U5.input_voltage, U6.O
  N26: S3.Pin_1, S3.Pin_2
  N27: Pololu_A3.1B, M5.A
  N28: Pololu_A3.1A, M5.C
  N29: Pololu_A3.2A, M5.B
  N30: Pololu_A3.2B, M5.D
  N31: Pololu_A3.VMOT, C3.+, Power_plug3.VCC, U6.P
  N32: LCD3.V0, R28.wiper
  N33: M6.A, IC3.Out_4
  N34: M6.C, IC3.Out_2
  N35: M6.B, IC3.Out_3
  N36: M6.D, IC3.Out_1
  N37: LED13.cathode, R33.Pin_0
  N38: LED14.cathode, R35.Pin_0
  N39: LED15.cathode, R34.Pin_0

notes:
  [GND, +, SW, DT, CLK]
  Microcontroller (Arduino Mega 2560)
  USB Serial I/O
  Z Stepper (17HS13-0404S)
  R Stepper (28BYJ-48)
  <= Z-Axis Stepper Controller (A4988)
  Turntable Stepper Controller (represents a ULN2003 breakout board)
  Click Encoder (represents 5-pin breakout)
  12V IN (Center +)
  Power Switch
  Ultrasonic Sensors (HC-SR04)
  Horizontal
  Vertical
  16x2 Text LCD
  Status LEDs
  3D Scanner
  Prototype v2.0 Wiring Diagram
  Z Limit Switch
  (contrast via 10KΩ pot)
  5V Auxiliary Rail
  (7805 Regulator)
  12V Rail
  (Direct from Jack)
  Switch-Controlled
  1µF
